# Fritzing sketch Full_down_switch (saved by Fritzing 0.9.3b)
breadboards: 1

parts:
  R1 = Resistor [tolerance=±5% resistance=220 package=THT]
  S1 = Pushbutton [package="[THT]"]
  부품1 = Arduino Uno (Rev3)

nets:
  N1: R1.Pin_1, 부품1.GND
  N2: S1.Pin_1, 부품1.D4
