# Fritzing sketch Full_up_switch (saved by Fritzing 0.9.3b)
breadboards: 1

parts:
  R1 = Resistor [tolerance=±5% resistance=220 package=THT]
  S1 = Pushbutton [package="[THT]"]
  부품1 = Arduino Uno (Rev3)

nets:
  N1: R1.Pin_0, 부품1.5V
  N2: R1.Pin_1, S1.Pin_3, S1.Pin_4
  N3: S1.Pin_2, 부품1.GND
