# Fritzing sketch INPUT_PULLUP_LED_ON_OFF_switch (saved by Fritzing 0.9.3b)
breadboards: 1

parts:
  S1 = Pushbutton [package="[THT]"]
  부품1 = Arduino Uno (Rev3)
  R1 = Resistor [tolerance=±5% resistance=220 package=THT]
  LED1 = LED - 5mm [color="Red (633nm)" package="5 mm [THT]"]

nets:
  N1: S1.Pin_2, 부품1.GND, LED1.cathode
  N2: S1.Pin_3, S1.Pin_4, 부품1.D7
  N3: 부품1.5V, R1.Pin_1
  N4: R1.Pin_0, LED1.anode
