# Fritzing sketch INPUT_PULLUP_switch (saved by Fritzing 0.9.3b)
breadboards: 1

parts:
  S1 = Pushbutton [package="[THT]"]
  부품1 = Arduino Uno (Rev3)

nets:
  N1: S1.Pin_2, 부품1.GND
  N2: S1.Pin_3, S1.Pin_4, 부품1.5V
