# Fritzing sketch digital_read_Serial (saved by Fritzing 0.9.3b)

parts:
  부품1 = Arduino Uno (Rev3)
  부품2 = Arduino Uno (Rev3)

nets:
  N1: 부품1.D7, 부품1.GND
  N2: 부품2.D7, 부품2.5V

notes:
  GND(0) read
  5V(1) read
