# Fritzing sketch floating_test (saved by Fritzing 0.9.3b)
breadboards: 1

parts:
  부품1 = Arduino Uno (Rev3)
  S1 = Pushbutton [package="[THT]"]

nets:
  N1: 부품1.GND, S1.Pin_3, S1.Pin_4
  N2: 부품1.D7, S1.Pin_1, S1.Pin_2
